# Fritzing sketch esquema MicroNano pcb 3 (saved by Fritzing 0.9.3b)
circuit board: 9.93033cm x 6.28741cm

parts:
  10K = Resistor [tolerance=±5% resistance=10k package=THT]
  10K_2 = Resistor [tolerance=±5% resistance=10k package=THT]
  J9 = female pin header, 2 pins [form="♀ (female)"]
  A5_a_13 = female pin header, 2 pins [form="♀ (female)"]
  J11 = female pin header, 2 pins [form="♀ (female)"]
  J12 = female pin header, 2 pins [form="♀ (female)"]
  J13 = female pin header, 2 pins [form="♀ (female)"]
  J14 = female pin header, 2 pins [form="♀ (female)"]
  4_a_11 = female pin header, 2 pins [form="♀ (female)"]
  J16 = female pin header, 2 pins [form="♀ (female)"]
  220 = Resistor [tolerance=±5% resistance=220 package=THT]
  220_2 = Resistor [tolerance=±5% resistance=220 package=THT]
  LED_negres = LED - 5mm [color="Red (633nm)" package="5 mm [THT]"]
  10k = Resistor [tolerance=±5% resistance=10k package=THT]
  10K_3 = Resistor [tolerance=±10% resistance=10k package=THT]
  RST = female pin header, 2 pins [form="♀ (female)"]
  s/m = female pin header, 2 pins [form="♀ (female)"]
  A_gnd = female pin header, 2 pins [form="♀ (female)"]
  btn_Jug = Toggle Switch [package=THT]
  5v_B = female pin header, 2 pins [form="♀ (female)"]
  MICRO = Arduino Micro (Rev3)
  GND = female pin header, 2 pins [form="♀ (female)"]
  Tx_Ok = female pin header, 2 pins [form="♀ (female)"]
  C_5V = female pin header, 2 pins [form="♀ (female)"]
  A_gnd_2 = female pin header, 2 pins [form="♀ (female)"]
  C_5V_2 = female pin header, 2 pins [form="♀ (female)"]
  DSP_Blanc2 = Grove 4 Digit Display
  NANO = Arduino Nano (Rev3.0)
  sck/miso = female pin header, 2 pins [form="♀ (female)"]
  Mosi_D = female pin header, 2 pins [form="♀ (female)"]
  Scl_Sda = female pin header, 2 pins [form="♀ (female)"]
  Rx = female pin header, 2 pins [form="♀ (female)"]
  D = female pin header, 2 pins [form="♀ (female)"]
  LED_blanques = LED - 5mm [color="Red (633nm)" package="5 mm [THT]"]
  Rx_D5 = female pin header, 2 pins [form="♀ (female)"]
  D5 = female pin header, 2 pins [form="♀ (female)"]
  J18 = female pin header, 2 pins [form="♀ (female)"]
  DSP_negre2 = Grove 4 Digit Display
  B_5v = female pin header, 2 pins [form="♀ (female)"]
  E_Tx = female pin header, 2 pins [form="♀ (female)"]

nets:
  N1: 10K.Pin_0, RST.pin1, MICRO.RESET
  5V: 10K.Pin_1, 10K_2.Pin_0, 10k.Pin_0, 10K_3.Pin_1, 5v_B.pin1, 5v_B.pin2, MICRO.5V, C_5V.pin1, C_5V.pin2, C_5V_2.pin1, C_5V_2.pin2, NANO.VIN, J18.pin1, J18.pin2, B_5v.pin1, B_5v.pin2
  N2: 10K_2.Pin_1, MICRO.D1/TX, Tx_Ok.pin1, NANO.D4, E_Tx.pin1
  N3: J9.pin1, MICRO.A4
  N4: J9.pin2, MICRO.A5
  N5: A5_a_13.pin1, MICRO.A2
  N6: A5_a_13.pin2, MICRO.A3
  N7: J11.pin1, MICRO.A0
  N8: J11.pin2, MICRO.A1
  N9: J12.pin1, MICRO.D13_PWM
  N10: J12.pin2, MICRO.D12_PWM/A11
  N11: J13.pin1, MICRO.D5_PWM
  N12: J13.pin2, MICRO.D4_PWM/A6
  N13: J14.pin1, MICRO.D7
  N14: J14.pin2, MICRO.D6_PWM/A7
  N15: 4_a_11.pin1, MICRO.D9_PWM/A9
  N16: 4_a_11.pin2, MICRO.D8_PWM/A8
  N17: J16.pin1, MICRO.D11_PWM
  N18: J16.pin2, MICRO.D10_PWM/A10
  GND: 220.Pin_0, 220_2.Pin_0, RST.pin2, s/m.pin2, A_gnd.pin1, A_gnd.pin2, btn_Jug.COM, MICRO.GND, GND.pin1, GND.pin2, Tx_Ok.pin2, A_gnd_2.pin1, A_gnd_2.pin2, DSP_Blanc2.GND, NANO.GND, DSP_negre2.GND
  N19: 220.Pin_1, LED_blanques.anode
  N20: 220_2.Pin_1, LED_negres.anode
  N21: LED_negres.cathode, NANO.A3
  N22: 10k.Pin_1, 10K_3.Pin_0, s/m.pin1, btn_Jug.L1, MICRO.D0/RX, NANO.D5, Rx.pin1, Rx.pin2, Rx_D5.pin1, Rx_D5.pin2, D5.pin1, D5.pin2, E_Tx.pin2
  N23: MICRO.MOSI, Mosi_D.pin2
  N24: MICRO.D2/SDA, Scl_Sda.pin2
  N25: MICRO.D3/SCL, Scl_Sda.pin1
  N26: MICRO.SCK, sck/miso.pin2
  N27: MICRO.MISO, sck/miso.pin1
  VCC: DSP_Blanc2.VCC, NANO.5V, DSP_negre2.VCC
  N28: DSP_Blanc2.DIO, NANO.A5, DSP_negre2.DIO
  N29: DSP_Blanc2.CLK, NANO.A4, DSP_negre2.CLK
  N30: NANO.D3, Mosi_D.pin1, D.pin1, D.pin2
  N31: NANO.A2, LED_blanques.cathode
